// Logisim project LEG.circ as structural Verilog: 4 circuits, main circuit main
module main (
);

  wire and_1_out, and_2_out, button_1_out, button_2_out, clock_1_out, decoder_1_out0, decoder_1_out1,
       decoder_1_out2, decoder_1_out3, decoder_2_out0, decoder_2_out1, decoder_2_out2, decoder_2_out3,
       decoder_3_out0, decoder_3_out1, decoder_3_out2, decoder_3_out3, decoder_4_out0, decoder_4_out1,
       decoder_4_out2, decoder_4_out3, decoder_5_out0, decoder_5_out1, decoder_5_out2, decoder_5_out3,
       decoder_6_out0, decoder_6_out1, decoder_6_out2, decoder_6_out3, demultiplexer_1_out0,
       demultiplexer_1_out1, multiplexer_5_out, not_1_out, not_3_out, not_4_out, not_5_out, or_1_out,
       or_2_out, or_3_out, or_4_out, or_8_1_out_2, or_8_out, or_9_out, smarter_register_1_p6,
       smarter_register_1_p8, smarter_register_1_p10, smarter_register_1_p15, smarter_register_1_p16,
       smarter_register_2_p6, smarter_register_2_p8, smarter_register_2_p10, smarter_register_2_p15,
       smarter_register_2_p16, smarter_register_3_p15, smarter_register_3_p16, smarter_register_4_clock_out,
       smarter_register_4_reset_out, smarter_register_5_p6, smarter_register_5_p8, smarter_register_5_p10,
       smarter_register_5_p15, smarter_register_5_p16, smarter_register_6_p6, smarter_register_6_p8,
       smarter_register_6_p10, smarter_register_6_p15, smarter_register_6_p16, smarter_register_7_p15,
       smarter_register_7_p16, smarter_register_8_clock_out, smarter_register_8_reset_out,
       smarter_register_9_p6, smarter_register_9_p8, smarter_register_9_p10, smarter_register_9_p15,
       smarter_register_9_p16, smarter_register_10_p6, smarter_register_10_p8, smarter_register_10_p10,
       smarter_register_10_p15, smarter_register_10_p16, smarter_register_11_p15, smarter_register_11_p16,
       smarter_register_12_clock_out, smarter_register_12_reset_out, smarter_register_13_p6,
       smarter_register_13_p8, smarter_register_13_p10, smarter_register_14_p6, smarter_register_14_p8,
       smarter_register_14_p10, subtractor_2_bout, xor_1_out, xor_2_out, xor_3_out;
  wire [1:0] rom_1_data_2, rom_1_data_4;
  wire [3:0] multiplexer_2_out, multiplexer_2_out_2, multiplexer_3_out, rom_1_data_6, rom_1_data_7,
       smarter_register_1_p5, smarter_register_1_p5_2;
  wire [7:0] adder_1_out, and_3_out, counter_1_q, divider_1_out, multiplexer_1_out, multiplier_1_out,
       nand_1_out, nor_1_out, not_2_out, or_5_out, or_6_out, or_7_out, register_1_q, rom_1_data,
       rom_1_data_3, rom_1_data_5, smarter_register_1_p7, smarter_register_1_p9, smarter_register_3_p6,
       smarter_register_3_p8, smarter_register_3_p10, smarter_register_5_p7, smarter_register_5_p9,
       smarter_register_7_p6, smarter_register_7_p8, smarter_register_7_p10, smarter_register_9_p7,
       smarter_register_9_p9, smarter_register_11_p6, smarter_register_11_p8, smarter_register_11_p10,
       smarter_register_13_p7, smarter_register_13_p9, smarter_register_15_p6, smarter_register_15_p8,
       smarter_register_15_p10, subtractor_1_out, xnor_1_out, xnor_2_out, xor_4_out;
  wire [7:4] multiplexer_3_out_2;

  ROM #(.dataWidth(32)) rom_1 (
    .addr(counter_1_q),
    .data({rom_1_data_7, rom_1_data_6, rom_1_data_5, rom_1_data_3[7:4], rom_1_data_4, rom_1_data_3[1:0], rom_1_data[7:4], rom_1_data_2, rom_1_data[1:0]}));
  and and_1 (and_1_out, rom_1_data_7[3], ~rom_1_data_7[2], rom_1_data_7[1], rom_1_data_7[0], rom_1_data_6[3], rom_1_data_6[2], rom_1_data_6[1], rom_1_data_6[0]);  // AND_Gate
  Decoder #(.select(2)) decoder_1 (
    .out0(decoder_1_out0), .out1(decoder_1_out1), .out2(decoder_1_out2), .out3(decoder_1_out3),
    .sel(rom_1_data_2), .en(xor_1_out));
  xor xor_1 (xor_1_out, rom_1_data[7], rom_1_data[4]);
  or or_1 (or_1_out, and_1_out, multiplexer_5_out);
  Decoder #(.select(2)) decoder_2 (
    .out0(decoder_2_out0), .out1(decoder_2_out1), .out2(decoder_2_out2), .out3(decoder_2_out3),
    .sel(rom_1_data_4), .en(xor_2_out));
  xor xor_2 (xor_2_out, or_2_out, rom_1_data_7[2]);
  or or_2 (or_2_out, rom_1_data_3[4], rom_1_data_7[2]);
  or or_3 (or_3_out, rom_1_data_5[4], rom_1_data_7[3]);
  Counter counter_1 (
    .load(or_1_out), .D(multiplexer_1_out), .Q(counter_1_q), .clk(or_4_out), .clr(button_1_out));  // open: count, carry, up
  Button button_1 (.out(button_1_out));
  or or_4 (or_4_out, button_2_out, clock_1_out);
  Button button_2 (.out(button_2_out));
  Register register_1 (
    .D({smarter_register_1_p5_2, smarter_register_1_p5}), .en(demultiplexer_1_out1), .clk(or_4_out),
    .Q(register_1_q), .clr(button_1_out));
  Decoder #(.select(2)) decoder_3 (
    .out0(decoder_3_out0), .out1(decoder_3_out1), .out2(decoder_3_out2), .out3(decoder_3_out3),
    .sel(rom_1_data_5[3:2]), .en(xor_3_out));
  Decoder #(.select(2)) decoder_4 (
    .out0(decoder_4_out0), .out1(decoder_4_out1), .out2(decoder_4_out2), .out3(decoder_4_out3),
    .sel(rom_1_data_5[1:0]), .en(xor_3_out));
  Decoder #(.select(2)) decoder_5 (
    .out0(decoder_5_out0), .out1(decoder_5_out1), .out2(decoder_5_out2), .out3(decoder_5_out3),
    .sel(rom_1_data_3[1:0]), .en(xor_2_out));
  Decoder #(.select(2)) decoder_6 (
    .out0(decoder_6_out0), .out1(decoder_6_out1), .out2(decoder_6_out2), .out3(decoder_6_out3),
    .sel(rom_1_data[1:0]), .en(xor_1_out));
  xor xor_3 (xor_3_out, or_3_out, rom_1_data_7[3]);
  Hex_Digit_Display hex_digit_display_1 (.value(rom_1_data_7));  // open: dp
  Clock clock_1 (.out(clock_1_out));
  Multiplexer #(.width(8)) multiplexer_1 (
    .in0(register_1_q), .in1({smarter_register_1_p5_2, smarter_register_1_p5}), .out(multiplexer_1_out),
    .sel(demultiplexer_1_out0));
  Hex_Digit_Display hex_digit_display_2 (.value(rom_1_data_6));  // open: dp
  Hex_Digit_Display hex_digit_display_3 (.value(rom_1_data_5[7:4]));  // open: dp
  Multiplexer #(.width(8)) multiplexer_2 (
    .in0(or_5_out), .in1({rom_1_data_3[7:4], rom_1_data_4, rom_1_data_3[1:0]}),
    .out({multiplexer_2_out_2, multiplexer_2_out}), .sel(rom_1_data_7[2]));
  Multiplexer #(.width(8)) multiplexer_3 (
    .in0(or_6_out), .in1(rom_1_data_5), .out({multiplexer_3_out_2, multiplexer_3_out}), .sel(rom_1_data_7[3]));
  assign or_5_out = smarter_register_1_p7 | smarter_register_5_p7 | smarter_register_9_p7 | smarter_register_13_p7;  // OR_Gate or_5, 8 bits wide
  // smarter_register smarter_register_1: pin names not known; wires that end beside it: decoder_6_out0, or_4_out, button_1_out, decoder_1_out0, {smarter_register_1_p5_2, smarter_register_1_p5}, smarter_register_1_p6, smarter_register_1_p7, smarter_register_1_p8, smarter_register_1_p9, smarter_register_1_p10, decoder_3_out0, decoder_2_out0, decoder_5_out0, decoder_4_out0, smarter_register_1_p15, smarter_register_1_p16
  // smarter_register smarter_register_2: pin names not known; wires that end beside it: decoder_6_out0, or_4_out, button_1_out, decoder_1_out1, smarter_register_1_p6, smarter_register_2_p6, smarter_register_1_p8, smarter_register_2_p8, smarter_register_1_p10, smarter_register_2_p10, decoder_3_out1, decoder_2_out1, decoder_5_out0, decoder_4_out0, smarter_register_2_p15, smarter_register_2_p16
  // smarter_register smarter_register_3: pin names not known; wires that end beside it: decoder_6_out0, or_4_out, button_1_out, decoder_1_out2, smarter_register_2_p6, smarter_register_3_p6, smarter_register_2_p8, smarter_register_3_p8, smarter_register_2_p10, smarter_register_3_p10, decoder_3_out2, decoder_2_out2, decoder_5_out0, decoder_4_out0, smarter_register_3_p15, smarter_register_3_p16
  smarter_register smarter_register_4 (
    .Clock_in(or_4_out), .Reset(button_1_out), .write_enable_a(decoder_1_out3),
    .write_enable_b(decoder_6_out0), .write_line_in(smarter_register_3_p6), .Opp_2_enable_a(decoder_2_out3),
    .Opp_1_enable_a(decoder_3_out3), .op_1_enable_b(decoder_4_out0), .op_2_enable_b(decoder_5_out0),
    .Operand_2(smarter_register_3_p8), .Operand_1(smarter_register_3_p10),
    .Reset_out(smarter_register_4_reset_out), .Clock_out(smarter_register_4_clock_out));  // open: Opp_2_in, Opp_1_in, write_line_out
  Hex_Digit_Display hex_digit_display_4 (.value(rom_1_data_5[3:0]));  // open: dp
  Hex_Digit_Display hex_digit_display_5 (.value(rom_1_data_3[7:4]));  // open: dp
  and and_2 (and_2_out, rom_1_data_7[0], rom_1_data_6[3], rom_1_data_6[2], rom_1_data_6[1], rom_1_data_6[0]);
  not not_1 (not_1_out, rom_1_data_7[1]);
  Demultiplexer demultiplexer_1 (
    .out0(demultiplexer_1_out0), .out1(demultiplexer_1_out1), .in(and_2_out), .sel(not_1_out));
  assign or_6_out = smarter_register_1_p9 | smarter_register_5_p9 | smarter_register_9_p9 | smarter_register_13_p9;  // OR_Gate or_6, 8 bits wide
  Hex_Digit_Display hex_digit_display_6 (.value({rom_1_data_4, rom_1_data_3[1:0]}));  // open: dp
  Hex_Digit_Display hex_digit_display_7 (.value(rom_1_data[7:4]));  // open: dp
  // smarter_register smarter_register_5: pin names not known; wires that end beside it: decoder_6_out1, smarter_register_1_p15, smarter_register_1_p16, decoder_1_out0, {smarter_register_1_p5_2, smarter_register_1_p5}, smarter_register_5_p6, smarter_register_5_p7, smarter_register_5_p8, smarter_register_5_p9, smarter_register_5_p10, decoder_3_out0, decoder_2_out0, decoder_5_out1, decoder_4_out1, smarter_register_5_p15, smarter_register_5_p16
  // smarter_register smarter_register_6: pin names not known; wires that end beside it: decoder_6_out1, smarter_register_2_p15, smarter_register_2_p16, decoder_1_out1, smarter_register_5_p6, smarter_register_6_p6, smarter_register_5_p8, smarter_register_6_p8, smarter_register_5_p10, smarter_register_6_p10, decoder_3_out1, decoder_2_out1, decoder_5_out1, decoder_4_out1, smarter_register_6_p15, smarter_register_6_p16
  // smarter_register smarter_register_7: pin names not known; wires that end beside it: decoder_6_out1, smarter_register_3_p15, smarter_register_3_p16, decoder_1_out2, smarter_register_6_p6, smarter_register_7_p6, smarter_register_6_p8, smarter_register_7_p8, smarter_register_6_p10, smarter_register_7_p10, decoder_3_out2, decoder_2_out2, decoder_5_out1, decoder_4_out1, smarter_register_7_p15, smarter_register_7_p16
  smarter_register smarter_register_8 (
    .Clock_in(smarter_register_4_clock_out), .Reset(smarter_register_4_reset_out),
    .write_enable_a(decoder_1_out3), .write_enable_b(decoder_6_out1), .write_line_in(smarter_register_7_p6),
    .Opp_2_enable_a(decoder_2_out3), .Opp_1_enable_a(decoder_3_out3), .op_1_enable_b(decoder_4_out1),
    .op_2_enable_b(decoder_5_out1), .Operand_2(smarter_register_7_p8), .Operand_1(smarter_register_7_p10),
    .Reset_out(smarter_register_8_reset_out), .Clock_out(smarter_register_8_clock_out));  // open: Opp_2_in, Opp_1_in, write_line_out
  Hex_Digit_Display hex_digit_display_8 (.value({rom_1_data_2, rom_1_data[1:0]}));  // open: dp
  // smarter_register smarter_register_9: pin names not known; wires that end beside it: decoder_6_out2, smarter_register_5_p15, smarter_register_5_p16, decoder_1_out0, {smarter_register_1_p5_2, smarter_register_1_p5}, smarter_register_9_p6, smarter_register_9_p7, smarter_register_9_p8, smarter_register_9_p9, smarter_register_9_p10, decoder_3_out0, decoder_2_out0, decoder_5_out2, decoder_4_out2, smarter_register_9_p15, smarter_register_9_p16
  // smarter_register smarter_register_10: pin names not known; wires that end beside it: decoder_6_out2, smarter_register_6_p15, smarter_register_6_p16, decoder_1_out1, smarter_register_9_p6, smarter_register_10_p6, smarter_register_9_p8, smarter_register_10_p8, smarter_register_9_p10, smarter_register_10_p10, decoder_3_out1, decoder_2_out1, decoder_5_out2, decoder_4_out2, smarter_register_10_p15, smarter_register_10_p16
  // smarter_register smarter_register_11: pin names not known; wires that end beside it: decoder_6_out2, smarter_register_7_p15, smarter_register_7_p16, decoder_1_out2, smarter_register_10_p6, smarter_register_11_p6, smarter_register_10_p8, smarter_register_11_p8, smarter_register_10_p10, smarter_register_11_p10, decoder_3_out2, decoder_2_out2, decoder_5_out2, decoder_4_out2, smarter_register_11_p15, smarter_register_11_p16
  smarter_register smarter_register_12 (
    .Clock_in(smarter_register_8_clock_out), .Reset(smarter_register_8_reset_out),
    .write_enable_a(decoder_1_out3), .write_enable_b(decoder_6_out2), .write_line_in(smarter_register_11_p6),
    .Opp_2_enable_a(decoder_2_out3), .Opp_1_enable_a(decoder_3_out3), .op_1_enable_b(decoder_4_out2),
    .op_2_enable_b(decoder_5_out2), .Operand_2(smarter_register_11_p8), .Operand_1(smarter_register_11_p10),
    .Reset_out(smarter_register_12_reset_out), .Clock_out(smarter_register_12_clock_out));  // open: Opp_2_in, Opp_1_in, write_line_out
  Hex_Digit_Display hex_digit_display_9 (.value(multiplexer_3_out));  // open: dp
  Hex_Digit_Display hex_digit_display_10 (.value(multiplexer_3_out_2));  // open: dp
  Hex_Digit_Display hex_digit_display_11 (.value(multiplexer_2_out_2));  // open: dp
  Hex_Digit_Display hex_digit_display_12 (.value(multiplexer_2_out));  // open: dp
  // smarter_register smarter_register_13: pin names not known; wires that end beside it: decoder_6_out3, smarter_register_9_p15, smarter_register_9_p16, decoder_1_out0, {smarter_register_1_p5_2, smarter_register_1_p5}, smarter_register_13_p6, smarter_register_13_p7, smarter_register_13_p8, smarter_register_13_p9, smarter_register_13_p10, decoder_3_out0, decoder_2_out0, decoder_4_out3, decoder_5_out3
  // smarter_register smarter_register_14: pin names not known; wires that end beside it: decoder_6_out3, smarter_register_10_p15, smarter_register_10_p16, decoder_1_out1, smarter_register_13_p6, smarter_register_14_p6, smarter_register_13_p8, smarter_register_14_p8, smarter_register_13_p10, smarter_register_14_p10, decoder_3_out1, decoder_2_out1, decoder_4_out3, decoder_5_out3
  // smarter_register smarter_register_15: pin names not known; wires that end beside it: decoder_6_out3, smarter_register_11_p15, smarter_register_11_p16, decoder_1_out2, smarter_register_14_p6, smarter_register_15_p6, smarter_register_14_p8, smarter_register_15_p8, smarter_register_14_p10, smarter_register_15_p10, decoder_3_out2, decoder_2_out2, decoder_4_out3, decoder_5_out3
  smarter_register smarter_register_16 (
    .Clock_in(smarter_register_12_clock_out), .Reset(smarter_register_12_reset_out),
    .write_enable_a(decoder_1_out3), .write_enable_b(decoder_6_out3), .write_line_in(smarter_register_15_p6),
    .Opp_2_enable_a(decoder_2_out3), .Opp_1_enable_a(decoder_3_out3), .op_1_enable_b(decoder_5_out3),
    .op_2_enable_b(decoder_4_out3), .Operand_2(smarter_register_15_p8), .Operand_1(smarter_register_15_p10));  // open: Opp_2_in, Opp_1_in, write_line_out, Reset_out, Clock_out
  Hex_Digit_Display hex_digit_display_13 (.value(smarter_register_1_p5_2));  // open: dp
  Hex_Digit_Display hex_digit_display_14 (.value(smarter_register_1_p5));  // open: dp
  Adder adder_1 (
    .a({multiplexer_3_out_2, multiplexer_3_out}), .b({multiplexer_2_out_2, multiplexer_2_out}),
    .out(adder_1_out));  // open: cin, cout
  Subtractor subtractor_1 (
    .a({multiplexer_3_out_2, multiplexer_3_out}), .b({multiplexer_2_out_2, multiplexer_2_out}),
    .out(subtractor_1_out));  // open: bin, bout
  Multiplier multiplier_1 (
    .a({multiplexer_3_out_2, multiplexer_3_out}), .b({multiplexer_2_out_2, multiplexer_2_out}),
    .out(multiplier_1_out));  // open: cin, cout
  Divider divider_1 (
    .a({multiplexer_3_out_2, multiplexer_3_out}), .b({multiplexer_2_out_2, multiplexer_2_out}),
    .out(divider_1_out));  // open: upper, rem
  assign not_2_out = ~{multiplexer_3_out_2, multiplexer_3_out};  // NOT_Gate not_2, 8 bits wide
  assign and_3_out = {multiplexer_2_out_2, multiplexer_2_out} & {multiplexer_3_out_2, multiplexer_3_out};  // AND_Gate and_3, 8 bits wide
  assign or_7_out = {multiplexer_2_out_2, multiplexer_2_out} | {multiplexer_3_out_2, multiplexer_3_out};  // OR_Gate or_7, 8 bits wide
  assign xor_4_out = {multiplexer_2_out_2, multiplexer_2_out} ^ {multiplexer_3_out_2, multiplexer_3_out};  // XOR_Gate xor_4, 8 bits wide
  RAM ram_1 (.sel(decoder_2_out1));  // open: addr, data, ld, clr
  assign nand_1_out = ~({multiplexer_2_out_2, multiplexer_2_out} & {multiplexer_3_out_2, multiplexer_3_out});  // NAND_Gate nand_1, 8 bits wide
  assign xnor_1_out = ~({multiplexer_2_out_2, multiplexer_2_out} ^ {multiplexer_3_out_2, multiplexer_3_out});  // XNOR_Gate xnor_1, 8 bits wide
  assign nor_1_out = ~({multiplexer_2_out_2, multiplexer_2_out} | {multiplexer_3_out_2, multiplexer_3_out});  // NOR_Gate nor_1, 8 bits wide
  Multiplexer #(.select(4), .width(8)) multiplexer_4 (
    .in0(adder_1_out), .in1(subtractor_1_out), .in2(multiplier_1_out), .in3(divider_1_out), .in4(not_2_out),
    .in5(nand_1_out), .in6(and_3_out), .in7(or_7_out), .in8(xor_4_out), .in9(xnor_1_out), .in10(nor_1_out),
    .in15(adder_1_out), .out({smarter_register_1_p5_2, smarter_register_1_p5}), .sel(rom_1_data_6));  // open: in11, in12, in13, in14
  Subtractor subtractor_2 (
    .a({multiplexer_3_out_2, multiplexer_3_out}), .b({multiplexer_2_out_2, multiplexer_2_out}),
    .bout(subtractor_2_bout));  // open: out, bin
  assign xnor_2_out = ~({multiplexer_2_out_2, multiplexer_2_out} ^ {multiplexer_3_out_2, multiplexer_3_out});  // XNOR_Gate xnor_2, 8 bits wide
  or_8 or_8_1 (.in_1(xnor_2_out), .out_2(or_8_1_out_2));
  not not_3 (not_3_out, or_8_1_out_2);
  or or_8 (or_8_out, or_8_1_out_2, subtractor_2_bout);
  or or_9 (or_9_out, ~subtractor_2_bout, or_8_1_out_2);  // OR_Gate
  Multiplexer #(.enable("true"), .select(3)) multiplexer_5 (
    .in0(1'b1), .in1(or_8_1_out_2), .in2(not_3_out), .in3(subtractor_2_bout), .in4(or_8_out),
    .in5(not_4_out), .in6(or_9_out), .in7(not_5_out), .out(multiplexer_5_out));  // open: sel, en
  not not_4 (not_4_out, subtractor_2_bout);
  not not_5 (not_5_out, 1'b1);

  // Notes on the sheet:
  //   contents of rom_1 (hex, n*v repeats v):
  //   bf0d000d
  //   Instruction
  //   Load_1
  //   Load_2
  //   Write_addr
  //   Operand_1
  //   Operand_2
  //   output
endmodule

module registers (
  input  [7:0] Write_Address,
  input  [7:0] Write_Line,
  input  [7:0] Operand_2_In,
  input  [7:0] Operand_1_In,
  input  Clock,
  input  [7:0] Instruction_Line,
  output [7:0] Operand_2_Out,
  output [7:0] Operand_1_Out
);

  wire and_1_out, and_2_out, and_3_out, and_4_out, and_5_out, and_6_out, and_7_out, and_8_out, button_1_out,
       decoder_1_out0, decoder_1_out1, decoder_1_out2, decoder_1_out3, decoder_2_out0, decoder_2_out1,
       decoder_3_out0, decoder_3_out1, decoder_3_out2, decoder_3_out3, or_1_out, undriven_3, undriven_4;
  wire [3:0] multiplexer_3_out, multiplexer_3_out_2, multiplexer_4_out, multiplexer_4_out_2;
  wire [7:0] controlled_buffer_1_out, controlled_buffer_2_out, controlled_buffer_3_out,
       controlled_buffer_4_out, controlled_buffer_5_out, controlled_buffer_6_out, controlled_buffer_7_out,
       controlled_buffer_8_out, controlled_buffer_9_out, controlled_buffer_10_out, controlled_buffer_11_out,
       controlled_buffer_12_out, register_9_q, register_10_q, register_11_q, register_12_q, undriven,
       undriven_2;

  Decoder #(.select(2)) decoder_1 (
    .out0(decoder_1_out0), .out1(decoder_1_out1), .out2(decoder_1_out2), .out3(decoder_1_out3));  // open: sel, en
  Multiplexer #(.width(8)) multiplexer_1 (
    .in0({multiplexer_4_out_2, multiplexer_4_out}), .in1(Operand_1_In), .out(Operand_1_Out),
    .sel(Instruction_Line[6]));
  Decoder #(.select(2)) decoder_2 (.out0(decoder_2_out0), .out1(decoder_2_out1));  // open: out2, out3, sel, en
  Multiplexer #(.width(8)) multiplexer_2 (
    .in0({multiplexer_3_out_2, multiplexer_3_out}), .in1(Operand_2_In), .out(Operand_2_Out),
    .sel(Instruction_Line[7]));
  assign controlled_buffer_1_out = and_1_out ? undriven : 8'bz;  // Controlled_Buffer controlled_buffer_1
  and and_1 (and_1_out, decoder_1_out0, decoder_2_out0);
  assign controlled_buffer_2_out = and_2_out ? undriven : 8'bz;  // Controlled_Buffer controlled_buffer_2
  and and_2 (and_2_out, decoder_1_out1, decoder_2_out0);
  assign controlled_buffer_3_out = and_3_out ? undriven : 8'bz;  // Controlled_Buffer controlled_buffer_3
  buf and_3 (and_3_out, decoder_1_out2);  // AND_Gate
  assign controlled_buffer_4_out = and_4_out ? undriven : 8'bz;  // Controlled_Buffer controlled_buffer_4
  and and_4 (and_4_out, decoder_1_out3, decoder_2_out0);
  Register register_1 (.D(controlled_buffer_1_out), .clk(undriven_3), .clr(undriven_4));  // open: en, Q
  Register register_2 (.D(controlled_buffer_2_out), .clk(undriven_3), .clr(undriven_4));  // open: en, Q
  Register register_3 (.D(controlled_buffer_3_out), .clk(undriven_3), .clr(undriven_4));  // open: en, Q
  Register register_4 (.D(controlled_buffer_4_out), .clk(undriven_3), .clr(undriven_4));  // open: en, Q
  Hex_Digit_Display hex_digit_display_1 (.value(Write_Line[7:4]));  // open: dp
  and and_5 (and_5_out, decoder_1_out0, decoder_2_out1);
  and and_6 (and_6_out, decoder_1_out1, decoder_2_out1);
  and and_7 (and_7_out, decoder_1_out2, decoder_2_out1);
  and and_8 (and_8_out, decoder_1_out3, decoder_2_out1);
  Hex_Digit_Display hex_digit_display_2 (.value(Write_Line[3:0]));  // open: dp
  assign controlled_buffer_5_out = and_5_out ? undriven_2 : 8'bz;  // Controlled_Buffer controlled_buffer_5
  Register register_5 (.D(controlled_buffer_5_out), .clk(undriven_3), .clr(undriven_4));  // open: en, Q
  assign controlled_buffer_6_out = and_6_out ? undriven_2 : 8'bz;  // Controlled_Buffer controlled_buffer_6
  Register register_6 (.D(controlled_buffer_6_out), .clk(undriven_3), .clr(undriven_4));  // open: en, Q
  assign controlled_buffer_7_out = and_7_out ? undriven_2 : 8'bz;  // Controlled_Buffer controlled_buffer_7
  Register register_7 (.D(controlled_buffer_7_out), .clk(undriven_3), .clr(undriven_4));  // open: en, Q
  assign controlled_buffer_8_out = and_8_out ? undriven_2 : 8'bz;  // Controlled_Buffer controlled_buffer_8
  Register register_8 (.D(controlled_buffer_8_out), .clk(undriven_3), .clr(undriven_4));  // open: en, Q
  Decoder #(.select(2)) decoder_3 (
    .out0(decoder_3_out0), .out1(decoder_3_out1), .out2(decoder_3_out2), .out3(decoder_3_out3),
    .sel(Write_Address[1:0]), .en(Write_Address[2]));
  assign controlled_buffer_9_out = decoder_3_out0 ? Write_Line : 8'bz;  // Controlled_Buffer controlled_buffer_9
  assign controlled_buffer_10_out = decoder_3_out1 ? Write_Line : 8'bz;  // Controlled_Buffer controlled_buffer_10
  assign controlled_buffer_11_out = decoder_3_out2 ? Write_Line : 8'bz;  // Controlled_Buffer controlled_buffer_11
  assign controlled_buffer_12_out = decoder_3_out3 ? Write_Line : 8'bz;  // Controlled_Buffer controlled_buffer_12
  Register register_9 (.D(controlled_buffer_9_out), .en(decoder_3_out0), .Q(register_9_q), .clk(Clock), .clr(or_1_out));
  Register register_10 (
    .D(controlled_buffer_10_out), .en(decoder_3_out1), .Q(register_10_q), .clk(Clock), .clr(or_1_out));
  Register register_11 (
    .D(controlled_buffer_11_out), .en(decoder_3_out2), .Q(register_11_q), .clk(Clock), .clr(or_1_out));
  Register register_12 (
    .D(controlled_buffer_12_out), .en(decoder_3_out3), .Q(register_12_q), .clk(Clock), .clr(or_1_out));
  or or_1 (or_1_out, Instruction_Line[0], button_1_out);
  Button button_1 (.out(button_1_out));
  Multiplexer #(.select(2), .width(8)) multiplexer_3 (
    .in0(register_9_q), .in1(register_10_q), .in2(register_11_q), .in3(register_12_q),
    .out({multiplexer_3_out_2, multiplexer_3_out}), .sel(Operand_2_In[1:0]));
  Multiplexer #(.select(2), .width(8)) multiplexer_4 (
    .in0(register_9_q), .in1(register_10_q), .in2(register_11_q), .in3(register_12_q),
    .out({multiplexer_4_out_2, multiplexer_4_out}), .sel(Operand_1_In[1:0]));
  Hex_Digit_Display hex_digit_display_3 (.value(multiplexer_3_out_2));  // open: dp
  Hex_Digit_Display hex_digit_display_4 (.value(multiplexer_4_out_2));  // open: dp
  Hex_Digit_Display hex_digit_display_5 (.value(multiplexer_3_out));  // open: dp
  Hex_Digit_Display hex_digit_display_6 (.value(multiplexer_4_out));  // open: dp
endmodule

module smarter_register (
  input  op_1_enable_b,
  input  [7:0] write_line_in,
  input  op_2_enable_b,
  input  write_enable_a,
  input  write_enable_b,
  input  Clock_in,
  input  Reset,
  input  [7:0] Opp_1_in,
  input  [7:0] Opp_2_in,
  input  Opp_2_enable_a,
  input  Opp_1_enable_a,
  output [7:0] Operand_2,
  output [7:0] Operand_1,
  output Clock_out,
  output Reset_out,
  output [7:0] write_line_out
);

  wire and_1_out, and_2_out, and_3_out;
  wire [7:0] controlled_buffer_1_out, register_1_q;

  and and_1 (and_1_out, write_enable_a, write_enable_b);
  assign controlled_buffer_1_out = and_1_out ? write_line_in : 8'bz;  // Controlled_Buffer controlled_buffer_1
  Register register_1 (.D(controlled_buffer_1_out), .en(and_1_out), .Q(register_1_q), .clk(Clock_in), .clr(Reset));
  LED Write_enable (.in(and_1_out));
  LED Op_enable (.in(and_2_out));
  and and_2 (and_2_out, op_2_enable_b, Opp_2_enable_a);
  Multiplexer #(.width(8)) multiplexer_1 (.in0(Opp_2_in), .in1(register_1_q), .out(Operand_2), .sel(and_2_out));
  Multiplexer #(.width(8)) multiplexer_2 (.in0(Opp_1_in), .in1(register_1_q), .out(Operand_1), .sel(and_3_out));
  and and_3 (and_3_out, Opp_1_enable_a, op_1_enable_b);
  LED Op1_enable (.in(and_3_out));

  assign Clock_out = Clock_in;
  assign Reset_out = Reset;
  assign write_line_out = write_line_in;
endmodule

module or_8 (
  input  [7:0] in_1,
  output out_2
);

  or or_1 (out_2, in_1[0], in_1[1], in_1[2], in_1[3], in_1[4], in_1[5], in_1[6], in_1[7]);
endmodule
